# Fritzing sketch lilka_fruit_piano (saved by Fritzing 1.0.7)

parts:
  Lilka1 = Lilka v2 (redraw) [part_number="Lilka v2"]
  Part4 = MPR121 Breakout

nets:
  N1: Lilka1.GPIO48, Part4.SCL
  N2: Lilka1.GPIO47, Part4.SDA
  3V3: Lilka1.3V3, Part4.3.3V
  GND: Lilka1.GND, Part4.GND

custom parts:
  Lilka v2 (redraw): Lilka v2 helper part for wiki screenshots. The breadboard view exposes the J2 extension header for connecting sensors and modules.
